// Logisim project Cache.circ as structural Verilog: 8 circuits, main circuit implementation
module implementation (
  input  [9:0] CpuAddressIn,
  input  CpuReadIn,
  input  CpuWriteIn,
  input  [7:0] CpuWriteValueIn,
  input  [31:0] LineFromMemIn,
  input  ClkIn,
  output ReadyOut,
  output DidContainOut,
  output [7:0] ByteReadOut,
  output [7:0] MemAddressOut,
  output MemReadOut,
  output MemWriteOut,
  output [31:0] Line2MemOut
);

  Cache cache_1 ();  // open: CpuAddressIn, CpuReadIn, CpuWriteIn, CpuWriteValueIn, LineFromMemIn, ClkIn, ReadyOut, DidContainOut, ByteReadOut, MemAddressOut, MemReadOut, MemWriteOut, Line2MemOut

  // Other names for the same wires on the sheet: clk = ClkIn; CpuAddress[9:0] = CpuAddressIn; CpuRead = CpuReadIn;
  //   CpuWrite = CpuWriteIn; CpuWriteValue[7:0] = CpuWriteValueIn; DidContain = DidContainOut;
  //   LineFromMem[31:0] = LineFromMemIn; MemAddress[7:0] = MemAddressOut; MemRead = MemReadOut;
  //   MemWrite = MemWriteOut; Ready = ReadyOut; ByteRead[7:0] = ByteReadOut; SelectedSetByteRead[7:0] = ByteReadOut;
  //   Line2Mem[31:0] = Line2MemOut; SelectedSetLine2Mem[31:0] = Line2MemOut
endmodule

module Cache (
  input  [9:0] CpuAddressIn,
  input  CpuReadIn,
  input  CpuWriteIn,
  input  [7:0] CpuWriteValueIn,
  input  [31:0] LineFromMemIn,
  input  ClkIn,
  output ReadyOut,
  output DidContainOut,
  output [7:0] ByteReadOut,
  output [7:0] MemAddressOut,
  output MemReadOut,
  output MemWriteOut,
  output [31:0] Line2MemOut
);

  wire CacheActive, CpuReadIn_t, CpuWriteIn_t, Initialize, not_2_out, SetBits, StoredCpuRead, StoredCpuWrite;
  wire [1:0] OffsetBits;
  wire [7:0] StoredCpuWriteValue;
  wire [9:3] StoredCpuAddress;

  Register #(.width(10)) register_1 (
    .D(CpuAddressIn), .en(ReadyOut), .clk(ClkIn), .Q({StoredCpuAddress, SetBits, OffsetBits}));  // open: clr
  Register #(.width(1)) register_2 (.D(CpuReadIn), .en(ReadyOut), .clk(ClkIn), .Q(StoredCpuRead));  // open: clr
  Register #(.width(1)) register_3 (.D(CpuWriteIn), .en(ReadyOut), .clk(ClkIn), .Q(StoredCpuWrite));  // open: clr
  Register register_4 (.D(CpuWriteValueIn), .en(ReadyOut), .clk(ClkIn), .Q(StoredCpuWriteValue));  // open: clr
  Multiplexer #(.enable("false")) multiplexer_1 (
    .in0(StoredCpuRead), .in1(CpuReadIn), .out(CpuReadIn_t), .sel(Initialize));
  Multiplexer #(.enable("false")) multiplexer_2 (
    .in0(StoredCpuWrite), .in1(CpuWriteIn), .out(CpuWriteIn_t), .sel(Initialize));
  not not_1 (CacheActive, ReadyOut);
  // AND_Gate and_1 has open pins: in0=CacheActive, in1=not_2_out, out=open
  not not_2 (not_2_out, SetBits);
  FSMController fsmcontroller_1 (
    .Read(CpuReadIn_t), .Write(CpuWriteIn_t), .Ready(ReadyOut), .Initialize(Initialize),
    .MemReadOut(MemReadOut), .MemWriteOut(MemWriteOut));  // open: didContain, Dirty
  Set set0 ();  // open: Active, Initialize, OffsetBits, TagBits, CpuReadIn, CpuWriteIn, CpuWriteValueIn, LineFromMemIn, ClkIn, DidContainOut, ByteReadOut, MemAddressOut, Line2MemOut
  Set set1 ();  // open: Active, Initialize, OffsetBits, TagBits, CpuReadIn, CpuWriteIn, CpuWriteValueIn, LineFromMemIn, ClkIn, DidContainOut, ByteReadOut, MemAddressOut, Line2MemOut

  // Other names for the same wires on the sheet: ByteRead[7:0] = ByteReadOut; clk = ClkIn;
  //   CpuAddress[9:0] = CpuAddressIn; CpuRead = CpuReadIn; CpuWrite = CpuWriteIn;
  //   CpuWriteValue[7:0] = CpuWriteValueIn; DidContain = DidContainOut; Line2Mem[31:0] = Line2MemOut;
  //   LineFromMem[31:0] = LineFromMemIn; MemAddress[7:0] = MemAddressOut; MemRead = MemReadOut;
  //   MemWrite = MemWriteOut; Ready = ReadyOut; StoredCpuAddress[2:0] = {SetBits, OffsetBits};
  //   TagBits[6:0] = StoredCpuAddress
endmodule

module Set (
  input  Active,
  input  Initialize,
  input  [1:0] OffsetBits,
  input  [6:0] TagBits,
  input  CpuReadIn,
  input  CpuWriteIn,
  input  [7:0] CpuWriteValueIn,
  input  [31:0] LineFromMemIn,
  input  ClkIn,
  output DidContainOut,
  output [7:0] ByteReadOut,
  output [7:0] MemAddressOut,
  output [31:0] Line2MemOut
);

  wire and_1_out, and_2_out, and_3_out, comparator_1_eq, comparator_2_eq, comparator_3_eq, inWay0, inWay1,
       inWay2, or_1_out, undriven, undriven_2, UpdateAge, Valid0, Valid1, Valid2;
  wire [1:0] Age0, Age0Out, Age1, Age1Out, Age2, Age2Out, AgeAccessed, multiplexer_1_out, multiplexer_2_out;
  wire [6:0] CurrTagBits0, CurrTagBits1, CurrTagBits2;

  Register #(.width(2)) u_age0 (.D(Age0Out), .en(or_1_out), .clk(ClkIn), .Q(Age0));  // open: clr
  or or_1 (or_1_out, Initialize, UpdateAge);
  Register #(.width(2)) u_age1 (.D(Age1Out), .en(undriven), .clk(ClkIn), .Q(Age1));  // open: clr
  Register #(.width(2)) u_age2 (.D(Age2Out), .en(undriven_2), .clk(ClkIn), .Q(Age2));  // open: clr
  AgeAccessedLogic ageaccessedlogic_1 (
    .AgeOfAccessed(AgeAccessed), .Age0(Age0), .Age1(Age1), .Age2(Age2), .Age0Out(Age0Out), .Age1Out(Age1Out),
    .Age2Out(Age2Out));
  Multiplexer #(.enable("false"), .width(2)) multiplexer_1 (
    .in0(2'b00), .in1(Age0), .out(multiplexer_1_out), .sel(inWay0));
  Comparator #(.width(7)) comparator_1 (.a(TagBits), .b(CurrTagBits0), .eq(comparator_1_eq));  // open: gt, lt
  Comparator #(.width(7)) comparator_2 (.a(TagBits), .b(CurrTagBits1), .eq(comparator_2_eq));  // open: gt, lt
  Comparator #(.width(7)) comparator_3 (.a(TagBits), .b(CurrTagBits2), .eq(comparator_3_eq));  // open: gt, lt
  Multiplexer #(.enable("false"), .width(2)) multiplexer_2 (
    .in0(multiplexer_1_out), .in1(Age1), .out(multiplexer_2_out), .sel(inWay1));
  Multiplexer #(.enable("false"), .width(2)) multiplexer_3 (
    .in0(multiplexer_2_out), .in1(Age2), .out(AgeAccessed), .sel(inWay2));
  Register #(.width(1)) register_1 (.D(and_1_out), .en(Initialize), .clk(ClkIn), .Q(inWay0));  // open: clr
  and and_1 (and_1_out, Valid0, comparator_1_eq);
  Register #(.width(1)) register_2 (.D(and_2_out), .en(Initialize), .clk(ClkIn), .Q(inWay1));  // open: clr
  and and_2 (and_2_out, Valid1, comparator_2_eq);
  Register #(.width(1)) register_3 (.D(and_3_out), .en(Initialize), .clk(ClkIn), .Q(inWay2));  // open: clr
  and and_3 (and_3_out, Valid2, comparator_3_eq);
  or or_2 (DidContainOut, inWay0, inWay1, inWay2);
  Way way0 (
    .CurrTagBits(CurrTagBits0), .Valid(Valid0));  // open: Active, TagBits, OffsetBits, CpuReadIn, CpuWriteIn, CpuWriteValueIn, LineFromMemIn, ClkIn, ByteReadOut, MemAddressOut, Line2MemOut
  Way way1 (
    .CurrTagBits(CurrTagBits1), .Valid(Valid1));  // open: Active, TagBits, OffsetBits, CpuReadIn, CpuWriteIn, CpuWriteValueIn, LineFromMemIn, ClkIn, ByteReadOut, MemAddressOut, Line2MemOut
  Way way2 (
    .CurrTagBits(CurrTagBits2), .Valid(Valid2));  // open: Active, TagBits, OffsetBits, CpuReadIn, CpuWriteIn, CpuWriteValueIn, LineFromMemIn, ClkIn, ByteReadOut, MemAddressOut, Line2MemOut

  // Other names for the same wires on the sheet: ByteRead[7:0] = ByteReadOut; clk = ClkIn; CpuRead = CpuReadIn;
  //   CpuWrite = CpuWriteIn; CpuWriteValue[7:0] = CpuWriteValueIn; DidContain = DidContainOut;
  //   Line2Mem[31:0] = Line2MemOut; LineFromMem[31:0] = LineFromMemIn; MemAddress[7:0] = MemAddressOut
endmodule

module Way (
  input  Active,
  input  [6:0] TagBits,
  input  [1:0] OffsetBits,
  input  CpuReadIn,
  input  CpuWriteIn,
  input  [7:0] CpuWriteValueIn,
  input  [31:0] LineFromMemIn,
  input  ClkIn,
  output [6:0] CurrTagBits,
  output Valid,
  output [7:0] ByteReadOut,
  output [7:0] MemAddressOut,
  output [31:0] Line2MemOut
);

  wire Dirty;
  wire [7:0] byte0out, byte1out, byte2out, byte3out;

  Register #(.width(1)) ValidReg (.Q(Valid));  // open: D, en, clk, clr
  Register #(.width(1)) DirtyReg (.Q(Dirty));  // open: D, en, clk, clr
  Register #(.width(7)) TagReg (.D(TagBits), .Q(CurrTagBits));  // open: en, clk, clr
  Register byte0 (.D(LineFromMemIn[7:0]), .Q(byte0out));  // open: en, clk, clr
  Register byte1 (.D(LineFromMemIn[15:8]), .Q(byte1out));  // open: en, clk, clr
  Register byte2 (.D(LineFromMemIn[23:16]), .Q(byte2out));  // open: en, clk, clr
  Register byte3 (.D(LineFromMemIn[31:24]), .Q(byte3out));  // open: en, clk, clr
  Multiplexer #(.enable("false"), .select(2), .width(8)) multiplexer_1 (
    .in0(byte0out), .in1(byte1out), .in2(byte2out), .in3(byte3out), .out(ByteReadOut), .sel(OffsetBits));

  // Other names for the same wires on the sheet: ByteRead[7:0] = ByteReadOut; clk = ClkIn; CpuRead = CpuReadIn;
  //   CpuWrite = CpuWriteIn; CpuWriteValue[7:0] = CpuWriteValueIn; Line2Mem[31:0] = Line2MemOut;
  //   byte0[7:0] = LineFromMemIn[7:0]; LineFromMem[31:0] = LineFromMemIn; byte1[7:0] = LineFromMemIn[15:8];
  //   byte2[7:0] = LineFromMemIn[23:16]; byte3[7:0] = LineFromMemIn[31:24]; MemAddress[7:0] = MemAddressOut
endmodule

module FSMController (
  input  Read,
  input  Write,
  input  didContain,
  input  Dirty,
  output Ready,
  output Initialize,
  output MemReadOut,
  output MemWriteOut
);

  wire [2:0] nextstate_1_nextstate, register_1_q;

  NextState nextstate_1 (
    .CurrentState(register_1_q), .Read(Read), .Write(Write), .didContain(didContain), .Dirty(Dirty),
    .NextState(nextstate_1_nextstate));
  Register #(.width(3)) register_1 (.D(nextstate_1_nextstate), .Q(register_1_q));  // open: en, clk, clr
  FSMOutput fsmoutput_1 (
    .State(register_1_q), .Ready(Ready), .Initialize(Initialize), .MemReadOut(MemReadOut),
    .MemWriteOut(MemWriteOut));
endmodule

module FSMOutput (
  input  [2:0] State,
  output Ready,
  output Initialize,
  output MemReadOut,
  output MemWriteOut
);

  wire not_1_out, not_2_out, not_3_out;

  not not_1 (not_1_out, State[2]);
  not not_2 (not_2_out, State[1]);
  not not_3 (not_3_out, State[0]);
  and and_1 (Ready, not_1_out, not_2_out, not_3_out);
  and and_2 (Initialize, not_1_out, not_2_out, State[0]);
  and and_3 (MemReadOut, State[2], State[1], not_3_out);
  and and_4 (MemWriteOut, not_1_out, State[1], not_3_out);
endmodule

module NextState (
  input  [2:0] CurrentState,
  input  Read,
  input  Write,
  input  didContain,
  input  Dirty,
  output [2:0] NextState
);

  wire and_1_out, and_2_out, and_3_out, and_4_out, and_5_out, and_6_out, and_7_out, and_8_out, and_9_out,
       and_10_out, not_1_out, not_2_out, not_3_out, not_4_out, not_5_out, not_6_out;

  not not_1 (not_1_out, CurrentState[2]);
  not not_2 (not_2_out, CurrentState[1]);
  not not_3 (not_3_out, CurrentState[0]);
  not not_4 (not_4_out, Read);
  not not_5 (not_5_out, didContain);
  not not_6 (not_6_out, Dirty);
  and and_1 (and_1_out, not_2_out, CurrentState[0], not_5_out, not_6_out);
  and and_2 (and_2_out, not_2_out, CurrentState[0], not_4_out, didContain);
  and and_3 (and_3_out, CurrentState[1], not_3_out);
  and and_4 (and_4_out, CurrentState[2], not_3_out, not_4_out);
  and and_5 (and_5_out, not_2_out, CurrentState[0]);
  and and_6 (and_6_out, not_1_out, CurrentState[1], not_3_out);
  or or_1 (NextState[1], and_5_out, and_6_out, and_7_out);
  and and_7 (and_7_out, CurrentState[2], not_2_out);
  and and_8 (and_8_out, not_2_out, not_3_out, Write);
  and and_9 (and_9_out, not_2_out, not_3_out, Read);
  or or_2 (NextState[0], and_8_out, and_9_out, and_10_out);
  and and_10 (and_10_out, not_2_out, CurrentState[0], didContain);
  or or_3 (NextState[2], and_1_out, and_2_out, and_3_out, and_4_out);
endmodule

module AgeAccessedLogic (
  input  [1:0] AgeOfAccessed,
  input  [1:0] Age0,
  input  [1:0] Age1,
  input  [1:0] Age2,
  output [1:0] Age0Out,
  output [1:0] Age1Out,
  output [1:0] Age2Out
);

  wire and_1_out, and_2_out, and_3_out, and_4_out, and_5_out, and_6_out, and_7_out, and_8_out, and_9_out,
       and_10_out, and_11_out, and_12_out, and_13_out, and_14_out, and_15_out, and_16_out, and_17_out,
       and_18_out, and_19_out, not_1_out, not_2_out, not_3_out, not_4_out, not_5_out, not_6_out, not_7_out;

  not not_1 (not_1_out, AgeOfAccessed[1]);
  not not_2 (not_2_out, AgeOfAccessed[0]);
  not not_3 (not_3_out, Age0[1]);
  not not_4 (not_4_out, Age0[0]);
  not not_5 (not_5_out, Age1[1]);
  not not_6 (not_6_out, Age2[1]);
  not not_7 (not_7_out, Age2[0]);
  and and_1 (and_1_out, not_1_out, Age0[1]);
  and and_2 (and_2_out, AgeOfAccessed[1], Age0[0]);
  and and_3 (and_3_out, not_1_out, not_2_out, Age0[0]);
  and and_4 (and_4_out, AgeOfAccessed[0], not_3_out, not_4_out);
  and and_5 (and_5_out, AgeOfAccessed[1], not_3_out, not_4_out);
  and and_6 (and_6_out, not_1_out, Age1[1]);
  and and_7 (and_7_out, AgeOfAccessed[1], not_4_out, not_7_out);
  and and_8 (and_8_out, not_1_out, not_2_out, not_4_out, not_7_out);
  and and_9 (and_9_out, AgeOfAccessed[0], not_5_out, Age2[0]);
  and and_10 (and_10_out, AgeOfAccessed[0], Age0[0], not_5_out);
  and and_11 (and_11_out, AgeOfAccessed[1], not_5_out, Age2[0]);
  and and_12 (and_12_out, AgeOfAccessed[1], Age0[0], not_5_out);
  and and_13 (and_13_out, not_1_out, not_3_out, not_5_out);
  and and_14 (and_14_out, AgeOfAccessed[1], Age2[0]);
  and and_15 (and_15_out, not_1_out, not_2_out, Age2[0]);
  and and_16 (and_16_out, AgeOfAccessed[0], Age1[0], not_6_out);
  and and_17 (and_17_out, AgeOfAccessed[0], Age0[0], not_6_out);
  and and_18 (and_18_out, AgeOfAccessed[1], Age1[0], not_6_out);
  and and_19 (and_19_out, AgeOfAccessed[1], Age0[0], not_6_out);
  or or_1 (Age0Out[1], and_1_out, and_2_out);
  or or_2 (Age0Out[0], and_3_out, and_4_out, and_5_out);
  or or_3 (Age1Out[1], and_6_out, and_7_out);
  or or_4 (Age1Out[0], and_8_out, and_9_out, and_10_out, and_11_out, and_12_out);
  or or_5 (Age2Out[1], and_13_out, and_14_out);
  or or_6 (Age2Out[0], and_15_out, and_16_out, and_17_out, and_18_out, and_19_out);
endmodule
